# Fritzing sketch fritzing_sensore (saved by Fritzing 0.9.3b)
breadboards: 1

parts:
  Componente1 = Arduino Uno (Rev3)
  U5 = RELAY [package=relay-jzc]
  J1 = Infrared Proximity Sensor

nets:
  N1: Componente1.D13/SCK, U5.COIL2
  N2: Componente1.D2, J1.Vout
  5V: Componente1.5V, U5.NC, J1.Vcc
  N3: Componente1.GND, U5.NO
